// Logisim project control-logic.circ as structural Verilog: 1 circuit, main circuit control_logic
module control_logic (
  input  [31:0] Instruction,
  input  BrEq,
  input  BrLt,
  output PCSel,
  output RegWEn,
  output [2:0] ImmSel,
  output BrUn,
  output ASel,
  output BSel,
  output [3:0] ALUSel,
  output MemRW,
  output [1:0] WBSel
);

  wire a0, a1, a2, a3, a4, a5, a6, a7, a8, a9, a10, a11, a12, a13, a14, a15, a16, a17, a18, a19, a20, a21,
       a22, a23, a24, a25, a26, a27, a28, a29, a30, a31, a32, a33, a34, a35, and_34_out, and_35_out,
       and_36_out, and_37_out, and_38_out, and_39_out, and_40_out, comparator_1_eq, comparator_2_eq,
       comparator_3_eq, comparator_4_eq, comparator_5_eq, comparator_6_eq, comparator_7_eq, comparator_8_eq,
       comparator_9_eq, comparator_10_eq, comparator_11_eq, comparator_12_eq, comparator_13_eq,
       comparator_14_eq, comparator_15_eq, comparator_16_eq, comparator_17_eq, comparator_18_eq,
       comparator_19_eq, comparator_20_eq, comparator_21_eq, comparator_22_eq, comparator_23_eq,
       comparator_24_eq, comparator_25_eq, comparator_26_eq, comparator_27_eq, comparator_28_eq,
       comparator_29_eq, comparator_30_eq, comparator_31_eq, comparator_32_eq, comparator_33_eq,
       comparator_34_eq, comparator_35_eq, comparator_36_eq, comparator_37_eq, comparator_38_eq,
       comparator_39_eq, comparator_40_eq, comparator_41_eq, comparator_42_eq, comparator_43_eq,
       comparator_44_eq, comparator_45_eq, comparator_46_eq, comparator_47_eq, comparator_48_eq,
       comparator_49_eq, comparator_50_eq, comparator_51_eq, comparator_52_eq, comparator_53_eq,
       comparator_54_eq, comparator_55_eq, comparator_56_eq, comparator_57_eq, comparator_58_eq,
       comparator_59_eq, comparator_60_eq, comparator_61_eq, comparator_62_eq, comparator_63_eq,
       comparator_64_eq, comparator_65_eq, comparator_66_eq, comparator_67_eq, comparator_68_eq,
       comparator_69_eq, comparator_70_eq, comparator_71_eq, comparator_72_eq, comparator_73_eq,
       comparator_74_eq, comparator_75_eq, comparator_76_eq, comparator_77_eq, comparator_78_eq,
       comparator_79_eq, comparator_81_eq, comparator_82_eq, comparator_85_eq, comparator_86_eq,
       comparator_87_eq, comparator_88_eq, comparator_89_eq, comparator_90_eq, comparator_91_eq,
       comparator_92_eq, comparator_93_eq, comparator_94_eq, comparator_95_eq, comparator_96_eq,
       comparator_97_eq, comparator_98_eq, comparator_99_eq, comparator_100_eq, not_1_out, not_2_out,
       not_3_out, or_1_out;
  wire [5:0] ROM_input;
  wire [15:14] rom_1_data;

  ROM #(.addrWidth(6), .dataWidth(16)) rom_1 (
    .addr(ROM_input), .data({rom_1_data, WBSel, MemRW, ALUSel, BSel, ASel, BrUn, ImmSel, RegWEn}));
  Comparator #(.width(7)) comparator_1 (.a(Instruction[6:0]), .b(7'b0010011), .eq(comparator_1_eq));  // open: gt, lt
  Comparator #(.width(3)) comparator_2 (.a(Instruction[14:12]), .b(3'b000), .eq(comparator_2_eq));  // open: gt, lt
  Comparator #(.width(7)) comparator_3 (.a(Instruction[6:0]), .b(7'b0010011), .eq(comparator_3_eq));  // open: gt, lt
  Comparator #(.width(3)) comparator_4 (.a(Instruction[14:12]), .b(3'b001), .eq(comparator_4_eq));  // open: gt, lt
  Comparator #(.width(7)) comparator_5 (.a(Instruction[31:25]), .b({7{1'b0}}), .eq(comparator_5_eq));  // open: gt, lt
  Comparator #(.width(7)) comparator_6 (.a(Instruction[6:0]), .b(7'b0010011), .eq(comparator_6_eq));  // open: gt, lt
  Comparator #(.width(3)) comparator_7 (.a(Instruction[14:12]), .b(3'b010), .eq(comparator_7_eq));  // open: gt, lt
  Comparator #(.width(7)) comparator_8 (.a(Instruction[6:0]), .b(7'b0010011), .eq(comparator_8_eq));  // open: gt, lt
  Comparator #(.width(3)) comparator_9 (.a(Instruction[14:12]), .b(3'b100), .eq(comparator_9_eq));  // open: gt, lt
  Comparator #(.width(7)) comparator_10 (.a(Instruction[6:0]), .b(7'b0010011), .eq(comparator_10_eq));  // open: gt, lt
  Comparator #(.width(3)) comparator_11 (.a(Instruction[14:12]), .b(3'b101), .eq(comparator_11_eq));  // open: gt, lt
  Comparator #(.width(7)) comparator_12 (.a(Instruction[31:25]), .b({7{1'b0}}), .eq(comparator_12_eq));  // open: gt, lt
  Comparator #(.width(7)) comparator_13 (.a(Instruction[6:0]), .b(7'b0010011), .eq(comparator_13_eq));  // open: gt, lt
  Comparator #(.width(3)) comparator_14 (.a(Instruction[14:12]), .b(3'b101), .eq(comparator_14_eq));  // open: gt, lt
  Comparator #(.width(7)) comparator_15 (
    .a(Instruction[31:25]), .b(7'b0100000), .eq(comparator_15_eq));  // open: gt, lt
  Comparator #(.width(7)) comparator_16 (.a(Instruction[6:0]), .b(7'b0010011), .eq(comparator_16_eq));  // open: gt, lt
  Comparator #(.width(3)) comparator_17 (.a(Instruction[14:12]), .b(3'b110), .eq(comparator_17_eq));  // open: gt, lt
  Comparator #(.width(7)) comparator_18 (.a(Instruction[6:0]), .b(7'b0010011), .eq(comparator_18_eq));  // open: gt, lt
  Comparator #(.width(3)) comparator_19 (.a(Instruction[14:12]), .b(3'b111), .eq(comparator_19_eq));  // open: gt, lt
  Comparator #(.width(7)) comparator_20 (.a(Instruction[6:0]), .b(7'b0110011), .eq(comparator_20_eq));  // open: gt, lt
  Comparator #(.width(3)) comparator_21 (.a(Instruction[14:12]), .b(3'b000), .eq(comparator_21_eq));  // open: gt, lt
  Comparator #(.width(7)) comparator_22 (.a(Instruction[31:25]), .b({7{1'b0}}), .eq(comparator_22_eq));  // open: gt, lt
  Comparator #(.width(7)) comparator_23 (.a(Instruction[6:0]), .b(7'b0110011), .eq(comparator_23_eq));  // open: gt, lt
  Comparator #(.width(3)) comparator_24 (.a(Instruction[14:12]), .b(3'b000), .eq(comparator_24_eq));  // open: gt, lt
  Comparator #(.width(7)) comparator_25 (
    .a(Instruction[31:25]), .b(7'b0000001), .eq(comparator_25_eq));  // open: gt, lt
  Comparator #(.width(7)) comparator_26 (.a(Instruction[6:0]), .b(7'b0110011), .eq(comparator_26_eq));  // open: gt, lt
  Comparator #(.width(3)) comparator_27 (.a(Instruction[14:12]), .b(3'b000), .eq(comparator_27_eq));  // open: gt, lt
  Comparator #(.width(7)) comparator_28 (
    .a(Instruction[31:25]), .b(7'b0100000), .eq(comparator_28_eq));  // open: gt, lt
  Comparator #(.width(7)) comparator_29 (.a(Instruction[6:0]), .b(7'b0110011), .eq(comparator_29_eq));  // open: gt, lt
  Comparator #(.width(3)) comparator_30 (.a(Instruction[14:12]), .b(3'b001), .eq(comparator_30_eq));  // open: gt, lt
  Comparator #(.width(7)) comparator_31 (.a(Instruction[31:25]), .b({7{1'b0}}), .eq(comparator_31_eq));  // open: gt, lt
  Comparator #(.width(7)) comparator_32 (.a(Instruction[6:0]), .b(7'b0110011), .eq(comparator_32_eq));  // open: gt, lt
  Comparator #(.width(3)) comparator_33 (.a(Instruction[14:12]), .b(3'b001), .eq(comparator_33_eq));  // open: gt, lt
  Comparator #(.width(7)) comparator_34 (
    .a(Instruction[31:25]), .b(7'b0000001), .eq(comparator_34_eq));  // open: gt, lt
  Comparator #(.width(7)) comparator_35 (.a(Instruction[6:0]), .b(7'b0110011), .eq(comparator_35_eq));  // open: gt, lt
  Comparator #(.width(3)) comparator_36 (.a(Instruction[14:12]), .b(3'b011), .eq(comparator_36_eq));  // open: gt, lt
  Comparator #(.width(7)) comparator_37 (
    .a(Instruction[31:25]), .b(7'b0000001), .eq(comparator_37_eq));  // open: gt, lt
  Comparator #(.width(7)) comparator_38 (.a(Instruction[6:0]), .b(7'b0110011), .eq(comparator_38_eq));  // open: gt, lt
  Comparator #(.width(3)) comparator_39 (.a(Instruction[14:12]), .b(3'b010), .eq(comparator_39_eq));  // open: gt, lt
  Comparator #(.width(7)) comparator_40 (.a(Instruction[31:25]), .b({7{1'b0}}), .eq(comparator_40_eq));  // open: gt, lt
  Comparator #(.width(7)) comparator_41 (.a(Instruction[6:0]), .b(7'b0110011), .eq(comparator_41_eq));  // open: gt, lt
  Comparator #(.width(3)) comparator_42 (.a(Instruction[14:12]), .b(3'b100), .eq(comparator_42_eq));  // open: gt, lt
  Comparator #(.width(7)) comparator_43 (.a(Instruction[31:25]), .b({7{1'b0}}), .eq(comparator_43_eq));  // open: gt, lt
  Comparator #(.width(7)) comparator_44 (.a(Instruction[6:0]), .b(7'b0110011), .eq(comparator_44_eq));  // open: gt, lt
  Comparator #(.width(3)) comparator_45 (.a(Instruction[14:12]), .b(3'b101), .eq(comparator_45_eq));  // open: gt, lt
  Comparator #(.width(7)) comparator_46 (.a(Instruction[31:25]), .b({7{1'b0}}), .eq(comparator_46_eq));  // open: gt, lt
  Comparator #(.width(7)) comparator_47 (.a(Instruction[6:0]), .b(7'b0110011), .eq(comparator_47_eq));  // open: gt, lt
  Comparator #(.width(3)) comparator_48 (.a(Instruction[14:12]), .b(3'b101), .eq(comparator_48_eq));  // open: gt, lt
  Comparator #(.width(7)) comparator_49 (
    .a(Instruction[31:25]), .b(7'b0100000), .eq(comparator_49_eq));  // open: gt, lt
  Comparator #(.width(7)) comparator_50 (.a(Instruction[6:0]), .b(7'b0110011), .eq(comparator_50_eq));  // open: gt, lt
  Comparator #(.width(3)) comparator_51 (.a(Instruction[14:12]), .b(3'b110), .eq(comparator_51_eq));  // open: gt, lt
  Comparator #(.width(7)) comparator_52 (.a(Instruction[31:25]), .b({7{1'b0}}), .eq(comparator_52_eq));  // open: gt, lt
  Comparator #(.width(7)) comparator_53 (.a(Instruction[6:0]), .b(7'b0110011), .eq(comparator_53_eq));  // open: gt, lt
  Comparator #(.width(3)) comparator_54 (.a(Instruction[14:12]), .b(3'b111), .eq(comparator_54_eq));  // open: gt, lt
  Comparator #(.width(7)) comparator_55 (.a(Instruction[31:25]), .b({7{1'b0}}), .eq(comparator_55_eq));  // open: gt, lt
  Comparator #(.width(7)) comparator_56 (.a(Instruction[6:0]), .b(7'b1100011), .eq(comparator_56_eq));  // open: gt, lt
  Comparator #(.width(3)) comparator_57 (.a(Instruction[14:12]), .b(3'b000), .eq(comparator_57_eq));  // open: gt, lt
  Comparator #(.width(7)) comparator_58 (.a(Instruction[6:0]), .b(7'b1100011), .eq(comparator_58_eq));  // open: gt, lt
  Comparator #(.width(3)) comparator_59 (.a(Instruction[14:12]), .b(3'b001), .eq(comparator_59_eq));  // open: gt, lt
  Comparator #(.width(7)) comparator_60 (.a(Instruction[6:0]), .b(7'b1100011), .eq(comparator_60_eq));  // open: gt, lt
  Comparator #(.width(3)) comparator_61 (.a(Instruction[14:12]), .b(3'b100), .eq(comparator_61_eq));  // open: gt, lt
  Comparator #(.width(7)) comparator_62 (.a(Instruction[6:0]), .b(7'b1100011), .eq(comparator_62_eq));  // open: gt, lt
  Comparator #(.width(3)) comparator_63 (.a(Instruction[14:12]), .b(3'b101), .eq(comparator_63_eq));  // open: gt, lt
  Comparator #(.width(7)) comparator_64 (.a(Instruction[6:0]), .b(7'b1100011), .eq(comparator_64_eq));  // open: gt, lt
  Comparator #(.width(3)) comparator_65 (.a(Instruction[14:12]), .b(3'b110), .eq(comparator_65_eq));  // open: gt, lt
  Comparator #(.width(7)) comparator_66 (.a(Instruction[6:0]), .b(7'b1100011), .eq(comparator_66_eq));  // open: gt, lt
  Comparator #(.width(3)) comparator_67 (.a(Instruction[14:12]), .b(3'b111), .eq(comparator_67_eq));  // open: gt, lt
  Comparator #(.width(7)) comparator_68 (.a(Instruction[6:0]), .b(7'b0000011), .eq(comparator_68_eq));  // open: gt, lt
  Comparator #(.width(3)) comparator_69 (.a(Instruction[14:12]), .b(3'b000), .eq(comparator_69_eq));  // open: gt, lt
  Comparator #(.width(7)) comparator_70 (.a(Instruction[6:0]), .b(7'b0000011), .eq(comparator_70_eq));  // open: gt, lt
  Comparator #(.width(3)) comparator_71 (.a(Instruction[14:12]), .b(3'b001), .eq(comparator_71_eq));  // open: gt, lt
  Comparator #(.width(7)) comparator_72 (.a(Instruction[6:0]), .b(7'b0000011), .eq(comparator_72_eq));  // open: gt, lt
  Comparator #(.width(3)) comparator_73 (.a(Instruction[14:12]), .b(3'b010), .eq(comparator_73_eq));  // open: gt, lt
  Comparator #(.width(7)) comparator_74 (.a(Instruction[6:0]), .b(7'b0100011), .eq(comparator_74_eq));  // open: gt, lt
  Comparator #(.width(3)) comparator_75 (.a(Instruction[14:12]), .b(3'b000), .eq(comparator_75_eq));  // open: gt, lt
  Comparator #(.width(7)) comparator_76 (.a(Instruction[6:0]), .b(7'b0100011), .eq(comparator_76_eq));  // open: gt, lt
  Comparator #(.width(3)) comparator_77 (.a(Instruction[14:12]), .b(3'b001), .eq(comparator_77_eq));  // open: gt, lt
  Comparator #(.width(7)) comparator_78 (.a(Instruction[6:0]), .b(7'b0100011), .eq(comparator_78_eq));  // open: gt, lt
  Comparator #(.width(3)) comparator_79 (.a(Instruction[14:12]), .b(3'b010), .eq(comparator_79_eq));  // open: gt, lt
  Comparator #(.width(7)) comparator_80 (.a(Instruction[6:0]), .b(7'b1101111), .eq(a34));  // open: gt, lt
  Comparator #(.width(7)) comparator_81 (.a(Instruction[6:0]), .b(7'b1100111), .eq(comparator_81_eq));  // open: gt, lt
  Comparator #(.width(3)) comparator_82 (.a(Instruction[14:12]), .b(3'b000), .eq(comparator_82_eq));  // open: gt, lt
  Comparator #(.width(7)) comparator_83 (.a(Instruction[6:0]), .b(7'b0010111), .eq(a32));  // open: gt, lt
  Comparator #(.width(7)) comparator_84 (.a(Instruction[6:0]), .b(7'b0110111), .eq(a33));  // open: gt, lt
  and and_1 (a15, comparator_1_eq, comparator_2_eq);
  and and_2 (a16, comparator_3_eq, comparator_4_eq, comparator_5_eq);
  and and_3 (a17, comparator_6_eq, comparator_7_eq);
  and and_4 (a18, comparator_8_eq, comparator_9_eq);
  and and_5 (a19, comparator_10_eq, comparator_11_eq, comparator_12_eq);
  and and_6 (a20, comparator_13_eq, comparator_14_eq, comparator_15_eq);
  and and_7 (a21, comparator_16_eq, comparator_17_eq);
  and and_8 (a22, comparator_18_eq, comparator_19_eq);
  and and_9 (a0, comparator_20_eq, comparator_21_eq, comparator_22_eq);
  and and_10 (a1, comparator_23_eq, comparator_24_eq, comparator_25_eq);
  and and_11 (a2, comparator_26_eq, comparator_27_eq, comparator_28_eq);
  and and_12 (a3, comparator_29_eq, comparator_30_eq, comparator_31_eq);
  and and_13 (a4, comparator_32_eq, comparator_33_eq, comparator_34_eq);
  and and_14 (a5, comparator_35_eq, comparator_36_eq, comparator_37_eq);
  and and_15 (a6, comparator_38_eq, comparator_39_eq, comparator_40_eq);
  and and_16 (a7, comparator_41_eq, comparator_42_eq, comparator_43_eq);
  and and_17 (a8, comparator_44_eq, comparator_45_eq, comparator_46_eq);
  and and_18 (a9, comparator_47_eq, comparator_48_eq, comparator_49_eq);
  and and_19 (a10, comparator_50_eq, comparator_51_eq, comparator_52_eq);
  and and_20 (a11, comparator_53_eq, comparator_54_eq, comparator_55_eq);
  and and_21 (a26, comparator_56_eq, comparator_57_eq);
  and and_22 (a27, comparator_58_eq, comparator_59_eq);
  and and_23 (a28, comparator_60_eq, comparator_61_eq);
  and and_24 (a29, comparator_62_eq, comparator_63_eq);
  and and_25 (a30, comparator_64_eq, comparator_65_eq);
  and and_26 (a31, comparator_66_eq, comparator_67_eq);
  and and_27 (a12, comparator_68_eq, comparator_69_eq);
  and and_28 (a13, comparator_70_eq, comparator_71_eq);
  and and_29 (a14, comparator_72_eq, comparator_73_eq);
  and and_30 (a23, comparator_74_eq, comparator_75_eq);
  and and_31 (a24, comparator_76_eq, comparator_77_eq);
  and and_32 (a25, comparator_78_eq, comparator_79_eq);
  and and_33 (a35, comparator_81_eq, comparator_82_eq);
  Comparator #(.width(7)) comparator_85 (.a(Instruction[6:0]), .b(7'b1100011), .eq(comparator_85_eq));  // open: gt, lt
  Comparator #(.width(3)) comparator_86 (.a(Instruction[14:12]), .b(3'b101), .eq(comparator_86_eq));  // open: gt, lt
  Comparator #(.width(7)) comparator_87 (.a(Instruction[6:0]), .b(7'b1100011), .eq(comparator_87_eq));  // open: gt, lt
  Comparator #(.width(3)) comparator_88 (.a(Instruction[14:12]), .b(3'b111), .eq(comparator_88_eq));  // open: gt, lt
  Comparator #(.width(7)) comparator_89 (.a(Instruction[6:0]), .b(7'b1101111), .eq(comparator_89_eq));  // open: gt, lt
  Comparator #(.width(7)) comparator_90 (.a(Instruction[6:0]), .b(7'b1101110), .eq(comparator_90_eq));  // open: gt, lt
  Comparator #(.width(7)) comparator_91 (.a(Instruction[6:0]), .b(7'b1100011), .eq(comparator_91_eq));  // open: gt, lt
  Comparator #(.width(3)) comparator_92 (.a(Instruction[14:12]), .b(3'b000), .eq(comparator_92_eq));  // open: gt, lt
  Comparator #(.width(7)) comparator_93 (.a(Instruction[6:0]), .b(7'b1100011), .eq(comparator_93_eq));  // open: gt, lt
  Comparator #(.width(3)) comparator_94 (.a(Instruction[14:12]), .b(3'b001), .eq(comparator_94_eq));  // open: gt, lt
  Comparator #(.width(7)) comparator_95 (.a(Instruction[6:0]), .b(7'b1100011), .eq(comparator_95_eq));  // open: gt, lt
  Comparator #(.width(3)) comparator_96 (.a(Instruction[14:12]), .b(3'b100), .eq(comparator_96_eq));  // open: gt, lt
  Comparator #(.width(7)) comparator_97 (.a(Instruction[6:0]), .b(7'b1100011), .eq(comparator_97_eq));  // open: gt, lt
  Comparator #(.width(3)) comparator_98 (.a(Instruction[14:12]), .b(3'b110), .eq(comparator_98_eq));  // open: gt, lt
  Comparator #(.width(7)) comparator_99 (.a(Instruction[6:0]), .b(7'b1100111), .eq(comparator_99_eq));  // open: gt, lt
  Comparator #(.width(3)) comparator_100 (.a(Instruction[14:12]), .b(3'b000), .eq(comparator_100_eq));  // open: gt, lt
  not not_1 (not_1_out, BrLt);
  not not_2 (not_2_out, BrLt);
  not not_3 (not_3_out, BrEq);
  and and_34 (and_34_out, comparator_85_eq, not_1_out, comparator_86_eq);
  and and_35 (and_35_out, comparator_87_eq, not_2_out, comparator_88_eq);
  or or_1 (or_1_out, comparator_89_eq, comparator_90_eq);
  and and_36 (and_36_out, comparator_91_eq, BrEq, comparator_92_eq);
  and and_37 (and_37_out, comparator_93_eq, not_3_out, comparator_94_eq);
  and and_38 (and_38_out, comparator_95_eq, BrLt, comparator_96_eq);
  and and_39 (and_39_out, comparator_97_eq, BrLt, comparator_98_eq);
  and and_40 (and_40_out, comparator_99_eq, comparator_100_eq);
  Priority_Encoder #(.select_enc(6)) priority_encoder_1 (
    .in0(a0), .in1(a1), .in2(a2), .in3(a3), .in4(a4), .in5(a5), .in6(a6), .in7(a7), .in8(a8), .in9(a9),
    .in10(a10), .in11(a11), .in12(a12), .in13(a13), .in14(a14), .in15(a15), .in16(a16), .in17(a17),
    .in18(a18), .in19(a19), .in20(a20), .in21(a21), .in22(a22), .in23(a23), .in24(a24), .in25(a25),
    .in26(a26), .in27(a27), .in28(a28), .in29(a29), .in30(a30), .in31(a31), .in32(a32), .in33(a33),
    .in34(a34), .in35(a35), .out(ROM_input));  // open: in36, in37, in38, in39, in40, in41, in42, in43, in44, in45, in46, in47, in48, in49, in50, in51, in52, in53, in54, in55, in56, in57, in58, in59, in60, in61, in62, in63, gs, en_out, en_in
  or or_2 (PCSel, and_34_out, and_35_out, or_1_out, and_36_out, and_37_out, and_38_out, and_39_out, and_40_out);

  // Notes on the sheet:
  //   INPUTS to your circuit
  //   Connect ROM Input here ->
  //   contents of rom_1 (hex, n*v repeats v):
  //   1001 1401 1601 1081 1481 1581 1101 1201 1281 1681 1301 1381 41 41 41 1041 10c1 1141 1241 12c1 16c1
  //   1341 13c1 1842 1842 1842 4*1064 1074 1074 1067 17e7 2069 2041
  //   ROM FOR CONTROL LOGIC
  //   DON'T CHANGE THE LOCATIONS OF THE INPUTS AND OUTPUTS!
  //   This is only if you choose to do the ROM option
  //   CONNECT
  //   WIRE
  //   TO
  //   USE
  //   ROM
  //   OUTPUT from your circuit
  //   Reminder: If using ROM, use combinational logic for PCSel
endmodule
