// Logisim project regfile.circ as structural Verilog: 1 circuit, main circuit regfile
module regfile (
  input  [4:0] ReadIndex1,
  input  [4:0] ReadIndex2,
  input  [4:0] WriteIndex,
  input  [31:0] WriteData,
  input  RegWEn,
  input  clk,
  output [31:0] ra,
  output [31:0] sp,
  output [31:0] t0,
  output [31:0] t1,
  output [31:0] t2,
  output [31:0] s0,
  output [31:0] s1,
  output [31:0] a0,
  output [31:0] ReadData1,
  output [31:0] ReadData2
);

  wire demultiplexer_1_out1, demultiplexer_1_out2, demultiplexer_1_out3, demultiplexer_1_out4,
       demultiplexer_1_out5, demultiplexer_1_out6, demultiplexer_1_out7, demultiplexer_1_out8,
       demultiplexer_1_out9, demultiplexer_1_out10, demultiplexer_1_out11, demultiplexer_1_out12,
       demultiplexer_1_out13, demultiplexer_1_out14, demultiplexer_1_out15, demultiplexer_1_out16,
       demultiplexer_1_out17, demultiplexer_1_out18, demultiplexer_1_out19, demultiplexer_1_out20,
       demultiplexer_1_out21, demultiplexer_1_out22, demultiplexer_1_out23, demultiplexer_1_out24,
       demultiplexer_1_out25, demultiplexer_1_out26, demultiplexer_1_out27, demultiplexer_1_out28,
       demultiplexer_1_out29, demultiplexer_1_out30, demultiplexer_1_out31, demultiplexer_2_out1,
       demultiplexer_2_out2, demultiplexer_2_out3, demultiplexer_2_out4, demultiplexer_2_out5,
       demultiplexer_2_out6, demultiplexer_2_out7, demultiplexer_2_out8, demultiplexer_2_out9,
       demultiplexer_2_out10, demultiplexer_2_out11, demultiplexer_2_out12, demultiplexer_2_out13,
       demultiplexer_2_out14, demultiplexer_2_out15, demultiplexer_2_out16, demultiplexer_2_out17,
       demultiplexer_2_out18, demultiplexer_2_out19, demultiplexer_2_out20, demultiplexer_2_out21,
       demultiplexer_2_out22, demultiplexer_2_out23, demultiplexer_2_out24, demultiplexer_2_out25,
       demultiplexer_2_out26, demultiplexer_2_out27, demultiplexer_2_out28, demultiplexer_2_out29,
       demultiplexer_2_out30, demultiplexer_2_out31;
  wire [31:0] register_3_q, register_4_q, register_11_q, register_12_q, register_13_q, register_14_q,
       register_15_q, register_16_q, register_17_q, register_18_q, register_19_q, register_20_q,
       register_21_q, register_22_q, register_23_q, register_24_q, register_25_q, register_26_q,
       register_27_q, register_28_q, register_29_q, register_30_q, register_31_q, register_34_q,
       register_35_q, register_42_q, register_43_q, register_44_q, register_45_q, register_46_q,
       register_47_q, register_48_q, register_49_q, register_50_q, register_51_q, register_52_q,
       register_53_q, register_54_q, register_55_q, register_56_q, register_57_q, register_58_q,
       register_59_q, register_60_q, register_61_q, register_62_q;

  Demultiplexer #(.select(5)) demultiplexer_1 (
    .out1(demultiplexer_1_out1), .out2(demultiplexer_1_out2), .out3(demultiplexer_1_out3),
    .out4(demultiplexer_1_out4), .out5(demultiplexer_1_out5), .out6(demultiplexer_1_out6),
    .out7(demultiplexer_1_out7), .out8(demultiplexer_1_out8), .out9(demultiplexer_1_out9),
    .out10(demultiplexer_1_out10), .out11(demultiplexer_1_out11), .out12(demultiplexer_1_out12),
    .out13(demultiplexer_1_out13), .out14(demultiplexer_1_out14), .out15(demultiplexer_1_out15),
    .out16(demultiplexer_1_out16), .out17(demultiplexer_1_out17), .out18(demultiplexer_1_out18),
    .out19(demultiplexer_1_out19), .out20(demultiplexer_1_out20), .out21(demultiplexer_1_out21),
    .out22(demultiplexer_1_out22), .out23(demultiplexer_1_out23), .out24(demultiplexer_1_out24),
    .out25(demultiplexer_1_out25), .out26(demultiplexer_1_out26), .out27(demultiplexer_1_out27),
    .out28(demultiplexer_1_out28), .out29(demultiplexer_1_out29), .out30(demultiplexer_1_out30),
    .out31(demultiplexer_1_out31), .in(RegWEn), .sel(WriteIndex));  // open: out0
  Register #(.width(32)) register_1 (.D(WriteData), .en(demultiplexer_1_out1), .clk(clk), .Q(ra));  // open: clr
  Register #(.width(32)) register_2 (.D(WriteData), .en(demultiplexer_1_out2), .clk(clk), .Q(sp));  // open: clr
  Register #(.width(32)) register_3 (
    .D(WriteData), .en(demultiplexer_1_out3), .clk(clk), .Q(register_3_q));  // open: clr
  Register #(.width(32)) register_4 (
    .D(WriteData), .en(demultiplexer_1_out4), .clk(clk), .Q(register_4_q));  // open: clr
  Register #(.width(32)) register_5 (.D(WriteData), .en(demultiplexer_1_out5), .clk(clk), .Q(t0));  // open: clr
  Register #(.width(32)) register_6 (.D(WriteData), .en(demultiplexer_1_out6), .clk(clk), .Q(t1));  // open: clr
  Register #(.width(32)) register_7 (.D(WriteData), .en(demultiplexer_1_out7), .clk(clk), .Q(t2));  // open: clr
  Register #(.width(32)) register_8 (.D(WriteData), .en(demultiplexer_1_out8), .clk(clk), .Q(s0));  // open: clr
  Register #(.width(32)) register_9 (.D(WriteData), .en(demultiplexer_1_out9), .clk(clk), .Q(s1));  // open: clr
  Register #(.width(32)) register_10 (.D(WriteData), .en(demultiplexer_1_out10), .clk(clk), .Q(a0));  // open: clr
  Register #(.width(32)) register_11 (
    .D(WriteData), .en(demultiplexer_1_out11), .clk(clk), .Q(register_11_q));  // open: clr
  Register #(.width(32)) register_12 (
    .D(WriteData), .en(demultiplexer_1_out12), .clk(clk), .Q(register_12_q));  // open: clr
  Register #(.width(32)) register_13 (
    .D(WriteData), .en(demultiplexer_1_out13), .clk(clk), .Q(register_13_q));  // open: clr
  Register #(.width(32)) register_14 (
    .D(WriteData), .en(demultiplexer_1_out14), .clk(clk), .Q(register_14_q));  // open: clr
  Register #(.width(32)) register_15 (
    .D(WriteData), .en(demultiplexer_1_out15), .clk(clk), .Q(register_15_q));  // open: clr
  Register #(.width(32)) register_16 (
    .D(WriteData), .en(demultiplexer_1_out16), .clk(clk), .Q(register_16_q));  // open: clr
  Register #(.width(32)) register_17 (
    .D(WriteData), .en(demultiplexer_1_out17), .clk(clk), .Q(register_17_q));  // open: clr
  Register #(.width(32)) register_18 (
    .D(WriteData), .en(demultiplexer_1_out18), .clk(clk), .Q(register_18_q));  // open: clr
  Register #(.width(32)) register_19 (
    .D(WriteData), .en(demultiplexer_1_out19), .clk(clk), .Q(register_19_q));  // open: clr
  Register #(.width(32)) register_20 (
    .D(WriteData), .en(demultiplexer_1_out20), .clk(clk), .Q(register_20_q));  // open: clr
  Register #(.width(32)) register_21 (
    .D(WriteData), .en(demultiplexer_1_out21), .clk(clk), .Q(register_21_q));  // open: clr
  Register #(.width(32)) register_22 (
    .D(WriteData), .en(demultiplexer_1_out22), .clk(clk), .Q(register_22_q));  // open: clr
  Register #(.width(32)) register_23 (
    .D(WriteData), .en(demultiplexer_1_out23), .clk(clk), .Q(register_23_q));  // open: clr
  Register #(.width(32)) register_24 (
    .D(WriteData), .en(demultiplexer_1_out24), .clk(clk), .Q(register_24_q));  // open: clr
  Register #(.width(32)) register_25 (
    .D(WriteData), .en(demultiplexer_1_out25), .clk(clk), .Q(register_25_q));  // open: clr
  Register #(.width(32)) register_26 (
    .D(WriteData), .en(demultiplexer_1_out26), .clk(clk), .Q(register_26_q));  // open: clr
  Register #(.width(32)) register_27 (
    .D(WriteData), .en(demultiplexer_1_out27), .clk(clk), .Q(register_27_q));  // open: clr
  Register #(.width(32)) register_28 (
    .D(WriteData), .en(demultiplexer_1_out28), .clk(clk), .Q(register_28_q));  // open: clr
  Register #(.width(32)) register_29 (
    .D(WriteData), .en(demultiplexer_1_out29), .clk(clk), .Q(register_29_q));  // open: clr
  Register #(.width(32)) register_30 (
    .D(WriteData), .en(demultiplexer_1_out30), .clk(clk), .Q(register_30_q));  // open: clr
  Register #(.width(32)) register_31 (
    .D(WriteData), .en(demultiplexer_1_out31), .clk(clk), .Q(register_31_q));  // open: clr
  Multiplexer #(.select(5), .width(32)) multiplexer_1 (
    .in0({32{1'b0}}), .in1(ra), .in2(sp), .in3(register_3_q), .in4(register_4_q), .in5(t0), .in6(t1),
    .in7(t2), .in8(s0), .in9(s1), .in10(a0), .in11(register_11_q), .in12(register_12_q),
    .in13(register_13_q), .in14(register_14_q), .in15(register_15_q), .in16(register_16_q),
    .in17(register_17_q), .in18(register_18_q), .in19(register_19_q), .in20(register_20_q),
    .in21(register_21_q), .in22(register_22_q), .in23(register_23_q), .in24(register_24_q),
    .in25(register_25_q), .in26(register_26_q), .in27(register_27_q), .in28(register_28_q),
    .in29(register_29_q), .in30(register_30_q), .in31(register_31_q), .out(ReadData2), .sel(ReadIndex2));
  Demultiplexer #(.select(5)) demultiplexer_2 (
    .out1(demultiplexer_2_out1), .out2(demultiplexer_2_out2), .out3(demultiplexer_2_out3),
    .out4(demultiplexer_2_out4), .out5(demultiplexer_2_out5), .out6(demultiplexer_2_out6),
    .out7(demultiplexer_2_out7), .out8(demultiplexer_2_out8), .out9(demultiplexer_2_out9),
    .out10(demultiplexer_2_out10), .out11(demultiplexer_2_out11), .out12(demultiplexer_2_out12),
    .out13(demultiplexer_2_out13), .out14(demultiplexer_2_out14), .out15(demultiplexer_2_out15),
    .out16(demultiplexer_2_out16), .out17(demultiplexer_2_out17), .out18(demultiplexer_2_out18),
    .out19(demultiplexer_2_out19), .out20(demultiplexer_2_out20), .out21(demultiplexer_2_out21),
    .out22(demultiplexer_2_out22), .out23(demultiplexer_2_out23), .out24(demultiplexer_2_out24),
    .out25(demultiplexer_2_out25), .out26(demultiplexer_2_out26), .out27(demultiplexer_2_out27),
    .out28(demultiplexer_2_out28), .out29(demultiplexer_2_out29), .out30(demultiplexer_2_out30),
    .out31(demultiplexer_2_out31), .in(RegWEn), .sel(WriteIndex));  // open: out0
  Register #(.width(32)) register_32 (.D(WriteData), .en(demultiplexer_2_out1), .clk(clk), .Q(ra));  // open: clr
  Register #(.width(32)) register_33 (.D(WriteData), .en(demultiplexer_2_out2), .clk(clk), .Q(sp));  // open: clr
  Register #(.width(32)) register_34 (
    .D(WriteData), .en(demultiplexer_2_out3), .clk(clk), .Q(register_34_q));  // open: clr
  Register #(.width(32)) register_35 (
    .D(WriteData), .en(demultiplexer_2_out4), .clk(clk), .Q(register_35_q));  // open: clr
  Register #(.width(32)) register_36 (.D(WriteData), .en(demultiplexer_2_out5), .clk(clk), .Q(t0));  // open: clr
  Register #(.width(32)) register_37 (.D(WriteData), .en(demultiplexer_2_out6), .clk(clk), .Q(t1));  // open: clr
  Register #(.width(32)) register_38 (.D(WriteData), .en(demultiplexer_2_out7), .clk(clk), .Q(t2));  // open: clr
  Register #(.width(32)) register_39 (.D(WriteData), .en(demultiplexer_2_out8), .clk(clk), .Q(s0));  // open: clr
  Register #(.width(32)) register_40 (.D(WriteData), .en(demultiplexer_2_out9), .clk(clk), .Q(s1));  // open: clr
  Register #(.width(32)) register_41 (.D(WriteData), .en(demultiplexer_2_out10), .clk(clk), .Q(a0));  // open: clr
  Register #(.width(32)) register_42 (
    .D(WriteData), .en(demultiplexer_2_out11), .clk(clk), .Q(register_42_q));  // open: clr
  Register #(.width(32)) register_43 (
    .D(WriteData), .en(demultiplexer_2_out12), .clk(clk), .Q(register_43_q));  // open: clr
  Register #(.width(32)) register_44 (
    .D(WriteData), .en(demultiplexer_2_out13), .clk(clk), .Q(register_44_q));  // open: clr
  Register #(.width(32)) register_45 (
    .D(WriteData), .en(demultiplexer_2_out14), .clk(clk), .Q(register_45_q));  // open: clr
  Register #(.width(32)) register_46 (
    .D(WriteData), .en(demultiplexer_2_out15), .clk(clk), .Q(register_46_q));  // open: clr
  Register #(.width(32)) register_47 (
    .D(WriteData), .en(demultiplexer_2_out16), .clk(clk), .Q(register_47_q));  // open: clr
  Register #(.width(32)) register_48 (
    .D(WriteData), .en(demultiplexer_2_out17), .clk(clk), .Q(register_48_q));  // open: clr
  Register #(.width(32)) register_49 (
    .D(WriteData), .en(demultiplexer_2_out18), .clk(clk), .Q(register_49_q));  // open: clr
  Register #(.width(32)) register_50 (
    .D(WriteData), .en(demultiplexer_2_out19), .clk(clk), .Q(register_50_q));  // open: clr
  Register #(.width(32)) register_51 (
    .D(WriteData), .en(demultiplexer_2_out20), .clk(clk), .Q(register_51_q));  // open: clr
  Register #(.width(32)) register_52 (
    .D(WriteData), .en(demultiplexer_2_out21), .clk(clk), .Q(register_52_q));  // open: clr
  Register #(.width(32)) register_53 (
    .D(WriteData), .en(demultiplexer_2_out22), .clk(clk), .Q(register_53_q));  // open: clr
  Register #(.width(32)) register_54 (
    .D(WriteData), .en(demultiplexer_2_out23), .clk(clk), .Q(register_54_q));  // open: clr
  Register #(.width(32)) register_55 (
    .D(WriteData), .en(demultiplexer_2_out24), .clk(clk), .Q(register_55_q));  // open: clr
  Register #(.width(32)) register_56 (
    .D(WriteData), .en(demultiplexer_2_out25), .clk(clk), .Q(register_56_q));  // open: clr
  Register #(.width(32)) register_57 (
    .D(WriteData), .en(demultiplexer_2_out26), .clk(clk), .Q(register_57_q));  // open: clr
  Register #(.width(32)) register_58 (
    .D(WriteData), .en(demultiplexer_2_out27), .clk(clk), .Q(register_58_q));  // open: clr
  Register #(.width(32)) register_59 (
    .D(WriteData), .en(demultiplexer_2_out28), .clk(clk), .Q(register_59_q));  // open: clr
  Register #(.width(32)) register_60 (
    .D(WriteData), .en(demultiplexer_2_out29), .clk(clk), .Q(register_60_q));  // open: clr
  Register #(.width(32)) register_61 (
    .D(WriteData), .en(demultiplexer_2_out30), .clk(clk), .Q(register_61_q));  // open: clr
  Register #(.width(32)) register_62 (
    .D(WriteData), .en(demultiplexer_2_out31), .clk(clk), .Q(register_62_q));  // open: clr
  Multiplexer #(.select(5), .width(32)) multiplexer_2 (
    .in0({32{1'b0}}), .in1(ra), .in2(sp), .in3(register_34_q), .in4(register_35_q), .in5(t0), .in6(t1),
    .in7(t2), .in8(s0), .in9(s1), .in10(a0), .in11(register_42_q), .in12(register_43_q),
    .in13(register_44_q), .in14(register_45_q), .in15(register_46_q), .in16(register_47_q),
    .in17(register_48_q), .in18(register_49_q), .in19(register_50_q), .in20(register_51_q),
    .in21(register_52_q), .in22(register_53_q), .in23(register_54_q), .in24(register_55_q),
    .in25(register_56_q), .in26(register_57_q), .in27(register_58_q), .in28(register_59_q),
    .in29(register_60_q), .in30(register_61_q), .in31(register_62_q), .out(ReadData1), .sel(ReadIndex1));

  // Notes on the sheet:
  //   INPUTS to your circuit
  //   DON'T CHANGE THE LOCATIONS OF THE INPUTS AND OUTPUTS!
  //   These are DEBUG/TEST outputs from your circuit.
  //   OUTPUTS from your circuit
endmodule
